# Fritzing sketch RefereeAndPlayer (saved by Fritzing 0.9.3b)

parts:
  Part1 = Arduino Nano (Rev3.0) (ICSP)
  HC-SR04_Sensor_1 = HC-SR04 Ultrasonic Distance Sensor
  HC-SR04_Sensor_2 = HC-SR04 Ultrasonic Distance Sensor
  HC-SR04_Sensor_3 = HC-SR04 Ultrasonic Distance Sensor
  U1 = Vibration Motor- ROB-08449 [package=vibe-motor-10mm]
  U2 = Vibration Motor- ROB-08449 [package=vibe-motor-10mm]
  U3 = Vibration Motor- ROB-08449 [package=vibe-motor-10mm]
  Rx2 = mystery part, 4 pins [chip_label=?]
  Part2 = Arduino Nano (Rev3.0) (ICSP)
  FC-1 = Sound Sensor
  Tx2 = mystery part, 3 pins [chip_label=?]
  BAT1 = BC9VPC [package=bc9vpc]
  BAT2 = BC9VPC [package=bc9vpc]

nets:
  N1: Part1.D2, HC-SR04_Sensor_1.TRIG
  N2: Part1.D3, HC-SR04_Sensor_1.ECHO
  N3: Part1.D4, HC-SR04_Sensor_2.TRIG
  N4: Part1.D5, U1.-
  N5: Part1.D6, U2.-
  N6: Part1.D7, HC-SR04_Sensor_2.ECHO
  N7: Part1.D8, HC-SR04_Sensor_3.TRIG
  N8: Part1.D9, HC-SR04_Sensor_3.ECHO
  N9: Part1.D11/MOSI, U3.-
  N10: Part1.D12/MISO, Rx2.pin2, Rx2.pin3
  N11: Part1.VIN, BAT1.V+
  GND: Part1.GND, HC-SR04_Sensor_1.GND, HC-SR04_Sensor_2.GND, HC-SR04_Sensor_3.GND, U1.+, U2.+, U3.+, Rx2.pin4, BAT1.V-
  VCC: Part1.5V, HC-SR04_Sensor_1.VCC, HC-SR04_Sensor_2.VCC, HC-SR04_Sensor_3.VCC, Rx2.pin1
  N12: Part2.D8, FC-1.OUT
  N13: Part2.D12/MISO, Tx2.pin1
  N14: Part2.VIN, BAT2.V+
  GND_2: Part2.GND, FC-1.GND, Tx2.pin3, BAT2.V-
  5V: Part2.5V, FC-1.VCC, Tx2.pin2

notes:
  Reciever
  Transmitter
