# Fritzing sketch RefereeAndPlayer_ver_1.0 (saved by Fritzing 0.9.3b)

parts:
  Part1 = Arduino Nano (Rev3.0) (ICSP)
  HC-SR04_Sensor_1 = HC-SR04 Ultrasonic Distance Sensor
  HC-SR04_Sensor_2 = HC-SR04 Ultrasonic Distance Sensor
  HC-SR04_Sensor_3 = HC-SR04 Ultrasonic Distance Sensor
  U1 = Vibration Motor- ROB-08449 [package=vibe-motor-10mm]
  U2 = Vibration Motor- ROB-08449 [package=vibe-motor-10mm]
  U3 = Vibration Motor- ROB-08449 [package=vibe-motor-10mm]
  Rx2 = mystery part, 4 pins [chip_label=?]
  Part2 = Arduino Nano (Rev3.0) (ICSP)
  FC-1 = Sound Sensor
  Tx2 = mystery part, 3 pins [chip_label=?]

nets:
  N1: Part1.D2, HC-SR04_Sensor_1.TRIG
  N2: Part1.D3, HC-SR04_Sensor_1.ECHO
  N3: Part1.D4, HC-SR04_Sensor_2.TRIG
  N4: Part1.D5, HC-SR04_Sensor_2.ECHO
  N5: Part1.D6, HC-SR04_Sensor_3.TRIG
  N6: Part1.D7, HC-SR04_Sensor_3.ECHO
  N7: Part1.D8, U1.-
  N8: Part1.D9, U2.-
  N9: Part1.D10, U3.-
  N10: Part1.D11/MOSI, Rx2.pin2
  GND: Part1.GND, HC-SR04_Sensor_1.GND, HC-SR04_Sensor_2.GND, HC-SR04_Sensor_3.GND, U1.+, U2.+, U3.+, Rx2.pin4
  VCC: Part1.5V, HC-SR04_Sensor_1.VCC, HC-SR04_Sensor_2.VCC, HC-SR04_Sensor_3.VCC, Rx2.pin1
  N11: Part2.D8, FC-1.OUT
  GND_2: Part2.GND, FC-1.GND, Tx2.pin3
  5V: Part2.5V, FC-1.VCC, Tx2.pin2

notes:
  Reciever
  Transmitter
